// Logisim project 6551071085_LAB1_4.circ as structural Verilog: 1 circuit, main circuit main
module main (
  input  [3:0] A,
  input  [3:0] B,
  output [3:0] Diff,
  output Borrow
);

  wire [3:0] not_1_out;

  assign not_1_out = ~B;  // NOT_Gate not_1, 4 bits wide
  Adder #(.width(4)) adder_1 (.a(A), .b(not_1_out), .out(Diff), .cin(1'b1), .cout(Borrow));

  // Notes on the sheet:
  //   Cao Trung Tính - 6551071085
endmodule
