// Logisim project 6551071085_LAB1_5.circ as structural Verilog: 1 circuit, main circuit main
module main (
  input  [3:0] A,
  input  [3:0] B,
  output out_3,
  output out_4,
  output out_5
);

  wire and_1_out, and_2_out, and_3_out, E0_out, E1_out, E2_out, E3_out, G0_out, G1_out, G2_out, G3_out,
       not_1_out, not_2_out, not_3_out, not_4_out;

  not not_1 (not_1_out, B[3]);
  not not_2 (not_2_out, B[2]);
  not not_3 (not_3_out, B[1]);
  not not_4 (not_4_out, B[0]);
  xnor E3 (E3_out, A[3], B[3]);
  xnor E2 (E2_out, A[2], B[2]);
  xnor E1 (E1_out, A[1], B[1]);
  xnor E0 (E0_out, A[0], B[0]);
  and G3 (G3_out, A[3], not_1_out);
  and G2 (G2_out, A[2], not_2_out);
  and G1 (G1_out, A[1], not_3_out);
  and G0 (G0_out, A[0], not_4_out);
  and A_B (out_3, E3_out, E2_out, E1_out, E0_out);
  and and_1 (and_1_out, E3_out, G2_out);
  and and_2 (and_2_out, E3_out, E2_out, G1_out);
  and and_3 (and_3_out, E3_out, E2_out, E1_out, G0_out);
  or A_B_2 (out_5, G3_out, and_1_out, and_2_out, and_3_out);
  nor A_B_3 (out_4, out_3, out_5);

  // Notes on the sheet:
  //   Cao Trung Tính - 6551071085
endmodule
