// Logisim project 6551071085_LAB1_7.circ as structural Verilog: 1 circuit, main circuit main
module main (
  input  [2:0] Address,
  input  [3:0] Data_In,
  input  Write_En,
  output [3:0] Data_Out
);

  wire clock_1_out;

  Clock clock_1 (.out(clock_1_out));
  RAM #(.addrWidth(3), .dataWidth(4), .bus("separate")) ram_1 (
    .addr(Address), .din(Data_In), .data(Data_Out), .str(Write_En), .sel(1'b1), .clk(clock_1_out), .ld(1'b1));  // open: clr

  // Notes on the sheet:
  //   Cao Trung Tính - 6551071085
endmodule
